# Fritzing sketch schema_multi_capteur (saved by Fritzing 0.9.2b)

parts:
  Composant1 = Arduino Uno (Rev3) - ICSP
  NRF24L1 = NRF24L01
  RHT1 = Humidity and Temperature Sensor RHT03
  Composant2 = Barometric Pressure Sensor - BMP085 Breakout
  DS1 = DS18B20 1-Wire Temperature Sensor [part_number=DS18B20]

nets:
  N1: Composant1.A4/SDA, Composant2.SDA
  N2: Composant1.A5/SCL, Composant2.SCL
  N3: Composant1.D9_PWM, NRF24L1.CE
  N4: Composant1.D10_PWM/SS, NRF24L1.CSN
  N5: Composant1.D11_PWM/MOSI, NRF24L1.MOSI
  N6: Composant1.D12/MISO, NRF24L1.MISO
  N7: Composant1.D13/SCK, NRF24L1.SCK
  N8: Composant1.D2, NRF24L1.IRQ
  N9: Composant1.D6_PWM, RHT1.Data-signal
  N10: Composant1.D7, DS1.DQ
  3V3: Composant1.3V3, NRF24L1.VCC
  5V: Composant1.5V, RHT1.Vcc
  GND: Composant1.GND, NRF24L1.GND

custom parts:
  NRF24L01: NRF24L01 module
